# Fritzing sketch v0.1a (saved by Fritzing 0.9.3b)
circuit board: 8.55cm x 5.4cm
breadboards: 1

parts:
  Atmega328P = atmega328 [package=dip]
  10K = Resistor [tolerance=±5% resistance=220 package=THT]
  +5V = Battery
  22p = Capacitor [package=cap-pth-small-kit]
  -_+ = Rectifier Diode [part_number=1N4001 package="300 mil [THT]"]
  0_1u = Ceramic Capacitor [capacitance=100nF package="100 mil [THT, multilayer]"]
  1K = Resistor [tolerance=±5% resistance=220 package=THT]
  USB = USB+SHIELD [package=usb-b-pth]
  + = Rectifier Diode [part_number=1N4001 package="300 mil [THT]"]
  SDK = LED - 5mm [color="Red (633nm)" package="5 mm [THT]"]
  R1-1K- = Resistor [tolerance=±5% resistance=1k package=THT]
  16Mhz = Crystal [frequency="16 Mhz" package=THT]
  USB-Serial = female pin header, 5 pins [form="♀ (female)"]
  5_•_6_•_7_•_8 = female pin header, 4 pins [form="♀ (female)"]
  L-ON = LED - 5mm [color="Red (633nm)" package="5 mm [THT]"]
  • = female pin header, 6 pins [form="♀ (female)"]
  13_12_11´10´_9´ = female pin header, 5 pins [form="♀ (female)"]
  A5_A4_A3_A2_A1_A0 = female pin header, 6 pins [form="♀ (female)"]
  S1 = Pushbutton [package="[THT]"]
  22p_2 = Capacitor [package=cap-pth-small-kit]

nets:
  N1: Atmega328P.RESET, 10K.Pin_1, 0_1u.0, •.pin1, S1.Pin_1, S1.Pin_2
  N2: Atmega328P.D0_(RX), USB-Serial.pin3, •.pin2
  N3: Atmega328P.D1_(TX), USB-Serial.pin4, •.pin3
  N4: Atmega328P.D2, •.pin4
  N5: Atmega328P.D3_(PWM), •.pin5
  N6: Atmega328P.D4, •.pin6
  N7: Atmega328P.VCC, Atmega328P.AVCC, Atmega328P.AREF, 10K.Pin_0, -_+.cathode, +.cathode, L-ON.anode
  GND: Atmega328P.GND, +5V.+, 22p.1, 1K.Pin_0, USB.GND, SDK.cathode, USB-Serial.pin1, S1.Pin_3, S1.Pin_4, 22p_2.1
  N8: Atmega328P.XLAT1, 22p.2, 16Mhz.pin_0
  N9: Atmega328P.XLAT2, 16Mhz.pin_1, 22p_2.2
  N10: Atmega328P.D5_(PWM), 5_•_6_•_7_•_8.pin1
  N11: Atmega328P.D6_(PWM), 5_•_6_•_7_•_8.pin2
  N12: Atmega328P.D7, 5_•_6_•_7_•_8.pin3
  N13: Atmega328P.D8, 5_•_6_•_7_•_8.pin4
  N14: Atmega328P.D9_(PWM), 13_12_11´10´_9´.pin5
  N15: Atmega328P.D10_(PWM), 13_12_11´10´_9´.pin4
  N16: Atmega328P.D11_(PWM), 13_12_11´10´_9´.pin3
  N17: Atmega328P.D12, 13_12_11´10´_9´.pin2
  N18: Atmega328P.D13, R1-1K-.Pin_0, 13_12_11´10´_9´.pin1
  N19: Atmega328P.A0, A5_A4_A3_A2_A1_A0.pin6
  N20: Atmega328P.A1, A5_A4_A3_A2_A1_A0.pin5
  N21: Atmega328P.A2, A5_A4_A3_A2_A1_A0.pin4
  N22: Atmega328P.A3, A5_A4_A3_A2_A1_A0.pin3
  N23: Atmega328P.A4, A5_A4_A3_A2_A1_A0.pin2
  N24: Atmega328P.A5, A5_A4_A3_A2_A1_A0.pin1
  N25: +5V.-, -_+.anode, USB.VBUS
  N26: 0_1u.1, USB-Serial.pin5
  N27: 1K.Pin_1, L-ON.cathode
  N28: +.anode, USB-Serial.pin2
  N29: SDK.anode, R1-1K-.Pin_1

notes:
  -
  +5Vcc
  GND
  RX TX
  SCL
  SDA
  arKDuino SMALL
  5V GND TX RX
  GND  VCC  TX  RX  DTR
  RST 0  1  2  3´ 4
